# Fritzing sketch PcbSetekiUltrasonicosAzules (saved by Fritzing 1.0.4)
circuit board: 19.0737cm x 13.9695cm
breadboards: 1

parts:
  J1 = Basic Servo
  M2 = DC Motor [voltage_(max)=6V voltage_(min)=3V]
  HC-SR04_Sensor_2 = HC-SR04 Ultrasonic Distance Sensor
  HC-SR04_Sensor_3 = HC-SR04 Ultrasonic Distance Sensor
  Componente1 = Motor Driver 1A Dual TB6612FNG
  J2 = Screw terminal - 2 pins [package=THT]  # not connected
  J3 = Screw terminal - 2 pins [package=THT]
  M3 = RioRand LM2596
  Componente3 = Arduino Nano (Rev3.0) (ICSP)
  S2 = Momentary Switch [package=ksa_sealed_tac_switch]
  U1 = SPDT Slide Switch [package=ayz0202]
  JP1 = Header 4 [package=screwterminal-3.5mm-4_lock]
  JP2 = Header 4 [package=screwterminal-3.5mm-4_lock]
  HC-SR04_Sensor_4 = HC-SR04 Ultrasonic Distance Sensor  # not connected
  JP3 = Header 4 [package=screwterminal-3.5mm-4_lock]
  J6 = female pin header, 2 pins [form="♀ (female)"]
  J7 = female pin header, 2 pins [form="♀ (female)"]
  J8 = female pin header, 2 pins [form="♀ (female)"]  # not connected
  J9 = female pin header, 2 pins [form="♀ (female)"]
  J10 = female pin header, 2 pins [form="♀ (female)"]
  J11 = female pin header, 2 pins [form="♀ (female)"]
  J12 = female pin header, 2 pins [form="♀ (female)"]
  J13 = female pin header, 2 pins [form="♀ (female)"]
  J14 = female pin header, 2 pins [form="♀ (female)"]

nets:
  GND: J1.gnd, HC-SR04_Sensor_2.GND, HC-SR04_Sensor_3.GND, Componente1.GND, M3.Pin_4, JP1.4, JP2.4, JP3.1, J6.pin1, J10.pin1, J10.pin2, J11.pin1, J13.pin2
  VCC: J1.vcc, HC-SR04_Sensor_2.VCC, HC-SR04_Sensor_3.VCC, Componente1.VCC, M3.Pin_3, Componente3.VIN, Componente3.5V, JP1.1, JP2.1, JP3.4, J11.pin2, J13.pin1
  N1: J1.pulse, Componente3.D8
  N2: M2.pin_2, Componente1.A01
  N3: HC-SR04_Sensor_2.TRIG, Componente3.D6, JP3.2
  N4: HC-SR04_Sensor_2.ECHO, Componente3.D7, JP3.3
  N5: HC-SR04_Sensor_3.TRIG, Componente3.D3, J9.pin2
  N6: HC-SR04_Sensor_3.ECHO, Componente3.D2, J9.pin1
  N7: Componente1.VM, M3.Pin_1, U1.6
  N8: Componente1.PWMA, Componente3.D9
  N9: Componente1.AIN2, Componente3.D10
  N10: Componente1.AIN1, Componente3.D11/MOSI
  N11: Componente1.STBY, Componente3.D12/MISO
  N12: J3.pin1, U1.3
  N13: J3.pin2, U1.4
  N14: M3.Pin_2, U1.1
  N15: Componente3.GND, S2.4
  N16: Componente3.D4, JP2.3
  N17: Componente3.D5, JP2.2
  N18: Componente3.A7, J12.pin2
  N19: Componente3.A6, J12.pin1
  N20: Componente3.A5, J7.pin2
  N21: Componente3.A4, J7.pin1
  N22: Componente3.A3, J14.pin2
  N23: Componente3.A2, JP1.2
  N24: Componente3.A1, JP1.3
  N25: Componente3.A0, S2.1
  N26: Componente3.3V3, J6.pin2
  N27: Componente3.D13/SCK, J14.pin1

notes:
  regulado a 5v
  entrada para la bateria 12 V
  derecho
  central
  izquierdo
  ==
  GY-BM008X
